# Fritzing sketch CG3002 (saved by Fritzing 0.9.3b)
stripboards: 2

parts:
  Arduino_Mega_2560 = Arduino Mega 2560 (Rev3)
  Raspberry_Pi_3 = Raspberry Pi 3 [part_number=RPI-3-V1.2]
  Level_Shifter = Logic Level Converter
  Part6 = INA169 Current Sensor Breakout [part_number=BOB-12040]
  R4 = Resistor [tolerance=±5% resistance=220 package="0402 [SMD]"]
  R5 = Resistor [tolerance=±5% resistance=220 package="0402 [SMD]"]
  BAT2 = Battery Holders [package=battery-aa]
  X2 = USB Connectors [package=usb-a-s-nosilk-female]
  X1 = USB Connectors [package=usb-a-s-nosilk-female]
  Back_Sensor = InvenSense MPU6050
  Forearm_Sensor = InvenSense MPU6050
  Hand_Sensor = InvenSense MPU6050

nets:
  N1: Arduino_Mega_2560.A0, Part6.VOUT
  N2: Arduino_Mega_2560.A1, R4.Pin_0, R5.Pin_1
  N3: Arduino_Mega_2560.D21/SCL, Back_Sensor.SCL, Forearm_Sensor.SCL, Hand_Sensor.SCL
  N4: Arduino_Mega_2560.D20/SDA, Back_Sensor.SDA, Forearm_Sensor.SDA, Hand_Sensor.SDA
  N5: Arduino_Mega_2560.D17_PWM/RX2, Level_Shifter.TX2_HV
  N6: Arduino_Mega_2560.D16_PWM/TX2, Level_Shifter.RX2_HV
  VCC: Arduino_Mega_2560.3V3, Back_Sensor.VCC, Forearm_Sensor.VCC, Hand_Sensor.VCC
  GND: Arduino_Mega_2560.GND, Raspberry_Pi_3.GND, Level_Shifter.GND, Back_Sensor.GND, Forearm_Sensor.GND, Hand_Sensor.GND
  N7: Arduino_Mega_2560.D2_PWM, Back_Sensor.AD0
  N8: Arduino_Mega_2560.D3_PWM, Forearm_Sensor.AD0
  N9: Arduino_Mega_2560.D4_PWM, Hand_Sensor.AD0
  N10: Arduino_Mega_2560.5V, Level_Shifter.HV
  N11: Raspberry_Pi_3.3v3, Level_Shifter.LV
  N12: Raspberry_Pi_3.GIPO15, Level_Shifter.RX2_LV
  N13: Raspberry_Pi_3.GIPO14, Level_Shifter.TX2_LV
  GND_2: Part6.GND, R5.Pin_0, BAT2.+, X2.GND, X1.GND
  N14: Part6.VIN+, R4.Pin_1
  N15: Part6.VIN-, X2.VBUS, X1.VBUS
  N16: Part6.VCC, BAT2.-

custom parts:
  INA169 Current Sensor Breakout: INA169 Current Sensor Breakout Board
